// Logisim project solution.circ as structural Verilog: 3 circuits, main circuit pipeline
// 2
module main (
  input  \сброс ,
  input  \направление ,
  input  \скорость 
);

  wire and_1_out, decoder_1_out0, decoder_1_out1, decoder_1_out2, decoder_1_out3, multiplexer_1_out,
       multiplexer_2_out, not_1_out, not_2_out, not_3_out, not_4_out, or_1_out, or_2_out, or_3_out,
       \АвтКонец , \заполненность , \захват , \остановка , \режим , \такт , \хват ;
  wire [1:0] \лапа ;
  wire [3:0] \pipeline_1_выход ;
  wire [4:0] multiplexer_3_out, multiplexer_3_out_2, multiplexer_3_out_3, multiplexer_3_out_4,
       multiplexer_3_out_5, multiplexer_5_out, multiplexer_5_out_2, multiplexer_5_out_3, multiplexer_5_out_4,
       multiplexer_5_out_5, multiplexer_7_out, multiplexer_7_out_2, multiplexer_7_out_3, multiplexer_7_out_4,
       multiplexer_7_out_5, multiplexer_9_out, multiplexer_9_out_2, multiplexer_9_out_3, multiplexer_9_out_4,
       multiplexer_11_out, multiplexer_11_out_2, multiplexer_11_out_3, multiplexer_11_out_4,
       multiplexer_11_out_5;
  wire [24:0] multiplexer_4_out, multiplexer_6_out, multiplexer_8_out, multiplexer_10_out;
  wire [24:20] multiplexer_9_out_5;

  Clock clock_1 (.out(\такт ));
  Button \u_хват  (.out(\хват ));
  not not_1 (not_1_out, \направление );
  or or_1 (or_1_out, \хват , \режим );
  not not_2 (not_2_out, \режим );
  not not_3 (not_3_out, \режим );
  Multiplexer #(.enable("false")) multiplexer_1 (.in0(1'b1), .in1(not_1_out), .out(multiplexer_1_out), .sel(not_3_out));
  Multiplexer #(.enable("false")) multiplexer_2 (
    .in0(1'b1), .in1(\скорость ), .out(multiplexer_2_out), .sel(not_3_out));
  D_Flip_Flop \u_режим  (.clk(\такт ), .D(or_2_out), .Q(\режим ), .reset(or_3_out));  // open: Qn, preset, en
  or or_2 (or_2_out, \захват , \заполненность );
  or or_3 (or_3_out, \АвтКонец , \сброс );
  D_Flip_Flop \u_захват  (.clk(or_1_out), .D(not_2_out), .Q(\захват ), .reset(\сброс ));  // open: Qn, preset, en
  Counter #(.width(2), .max('h3)) counter_1 (
    .load(multiplexer_1_out), .D(\лапа ), .count(multiplexer_2_out), .Q(\лапа ), .clk(\такт ));  // open: carry, clr
  and and_1 (and_1_out, ~\лапа [0], ~\лапа [1]);  // AND_Gate
  and and_2 (\АвтКонец , and_1_out, \режим );
  Decoder #(.select(2), .disabled(0), .enable("false")) decoder_1 (
    .out0(decoder_1_out0), .out1(decoder_1_out1), .out2(decoder_1_out2), .out3(decoder_1_out3), .sel(\лапа ));
  LED _0 (.in(\pipeline_1_выход [0]));
  DotMatrix #(.matrixrows(5)) dotmatrix_1 (
    .col0(multiplexer_3_out_5), .col1(multiplexer_3_out_4), .col2(multiplexer_3_out_3),
    .col3(multiplexer_3_out_2), .col4(multiplexer_3_out));
  DotMatrix #(.matrixrows(5)) dotmatrix_2 (
    .col0(multiplexer_5_out_5), .col1(multiplexer_5_out_4), .col2(multiplexer_5_out_3),
    .col3(multiplexer_5_out_2), .col4(multiplexer_5_out));
  Multiplexer #(.width(25), .enable("false")) multiplexer_3 (
    .in0({25{1'b0}}), .in1(multiplexer_4_out),
    .out({multiplexer_3_out_5, multiplexer_3_out_4, multiplexer_3_out_3, multiplexer_3_out_2, multiplexer_3_out}),
    .sel(decoder_1_out0));
  Multiplexer #(.width(25), .enable("false")) multiplexer_4 (
    .in0(25'h1f0843f), .in1(25'h1f0943f), .out(multiplexer_4_out), .sel(\заполненность ));
  pipeline pipeline_1 (
    .\АвтКонец (\АвтКонец ), .\сброс (\сброс ), .\такт (\такт ), .\остановка (\остановка ),
    .\захват (\захват ), .\лапа (\лапа ), .\выход (\pipeline_1_выход ), .\заполненность (\заполненность ));
  LED _1 (.in(\pipeline_1_выход [1]));
  LED _2 (.in(\pipeline_1_выход [2]));
  DotMatrix #(.matrixrows(5)) dotmatrix_3 (
    .col0(multiplexer_7_out_5), .col1(multiplexer_7_out_4), .col2(multiplexer_7_out_3),
    .col3(multiplexer_7_out_2), .col4(multiplexer_7_out));
  Multiplexer #(.width(25), .enable("false")) multiplexer_5 (
    .in0({25{1'b0}}), .in1(multiplexer_6_out),
    .out({multiplexer_5_out_5, multiplexer_5_out_4, multiplexer_5_out_3, multiplexer_5_out_2, multiplexer_5_out}),
    .sel(decoder_1_out1));
  Multiplexer #(.width(25), .enable("false")) multiplexer_6 (
    .in0(25'h1f0843f), .in1(25'h1f0943f), .out(multiplexer_6_out), .sel(\заполненность ));
  LED _3 (.in(\pipeline_1_выход [3]));
  DotMatrix #(.matrixrows(5)) dotmatrix_4 (
    .col0(multiplexer_9_out_5), .col1(multiplexer_9_out_4), .col2(multiplexer_9_out_3),
    .col3(multiplexer_9_out_2), .col4(multiplexer_9_out));
  Multiplexer #(.width(25), .enable("false")) multiplexer_7 (
    .in0({25{1'b0}}), .in1(multiplexer_8_out),
    .out({multiplexer_7_out_5, multiplexer_7_out_4, multiplexer_7_out_3, multiplexer_7_out_2, multiplexer_7_out}),
    .sel(decoder_1_out2));
  Multiplexer #(.width(25), .enable("false")) multiplexer_8 (
    .in0(25'h1f0843f), .in1(25'h1f0943f), .out(multiplexer_8_out), .sel(\заполненность ));
  LED \u_остановка  (.in(\остановка ));
  LED \u_захват_2  (.in(\захват ));
  DotMatrix #(.matrixrows(5)) dotmatrix_5 (
    .col0(multiplexer_11_out_5), .col1(multiplexer_11_out_4), .col2(multiplexer_11_out_3),
    .col3(multiplexer_11_out_2), .col4(multiplexer_11_out));
  Multiplexer #(.width(25), .enable("false")) multiplexer_9 (
    .in0({25{1'b0}}), .in1(multiplexer_10_out),
    .out({multiplexer_9_out_5, multiplexer_9_out_4, multiplexer_9_out_3, multiplexer_9_out_2, multiplexer_9_out}),
    .sel(decoder_1_out3));
  Multiplexer #(.width(25), .enable("false")) multiplexer_10 (
    .in0(25'h1f0843f), .in1(25'h1f0943f), .out(multiplexer_10_out), .sel(\заполненность ));
  LED \u_заполненность  (.in(\заполненность ));
  or or_4 (\остановка , \захват , \режим );
  not not_4 (not_4_out, \направление );
  Multiplexer #(.width(25), .enable("false")) multiplexer_11 (
    .in0(25'h4255c4), .in1(25'h475484),
    .out({multiplexer_11_out_5, multiplexer_11_out_4, multiplexer_11_out_3, multiplexer_11_out_2, multiplexer_11_out}),
    .sel(not_4_out));

  // Other names for the same wires on the sheet: стрелка = \направление 
endmodule

// Конвейер
module pipeline (
  input  \АвтКонец ,
  input  \сброс ,
  input  \такт ,
  input  \остановка ,
  input  \захват ,
  input  [1:0] \лапа ,
  output \заполненность ,
  output [3:0] \выход 
);

  wire and_1_out, and_2_out, and_3_out, or_1_out, or_2_out, or_3_out;
  wire [3:0] and_4_out, decoder_1_out0;

  and and_1 (and_1_out, ~\остановка , ~\захват );  // AND_Gate
  and and_2 (and_2_out, \захват , ~\заполненность );  // AND_Gate
  Decoder #(.select(2), .disabled(0)) decoder_1 (
    .out0(decoder_1_out0[0]), .out1(decoder_1_out0[1]), .out2(decoder_1_out0[2]), .out3(decoder_1_out0[3]),
    .sel(\лапа ), .en(and_2_out));
  and and_3 (and_3_out, \такт , and_1_out);
  D_Flip_Flop d_ff_1 (
    .clk(and_3_out), .D(\выход [3]), .Q(\выход [0]), .preset(\сброс ), .reset(and_4_out[0]));  // open: Qn, en
  assign and_4_out = decoder_1_out0 & \выход ;  // AND_Gate and_4, 4 bits wide
  D_Flip_Flop d_ff_2 (
    .clk(and_3_out), .D(\выход [0]), .Q(\выход [1]), .preset(\сброс ), .reset(and_4_out[1]));  // open: Qn, en
  or or_1 (or_1_out, and_4_out[0], and_4_out[1], and_4_out[2], and_4_out[3]);
  D_Flip_Flop d_ff_3 (
    .clk(and_3_out), .D(\выход [1]), .Q(\выход [2]), .preset(\сброс ), .reset(and_4_out[2]));  // open: Qn, en
  D_Flip_Flop \u_заполн  (.clk(or_1_out), .D(or_1_out), .Q(\заполненность ), .reset(or_3_out));  // open: Qn, preset, en
  D_Flip_Flop d_ff_4 (.clk(and_3_out), .D(\выход [2]), .Q(\выход [3]), .reset(or_2_out));  // open: Qn, preset, en
  or or_2 (or_2_out, \сброс , and_4_out[3]);
  or or_3 (or_3_out, \сброс , \АвтКонец );
endmodule

module test (
  input  [1:0] in_1
);

  wire clock_1_out;
  wire [1:0] counter_1_q;

  Clock clock_1 (.out(clock_1_out));
  Counter #(.width(2), .max('h3)) counter_1 (
    .load(1'b1), .D(in_1), .count(1'b0), .Q(counter_1_q), .clk(clock_1_out));  // open: carry, clr
endmodule
