// Logisim project source.circ as structural Verilog: 1 circuit, main circuit main
module main (
  input  \сброс ,
  input  \направление ,
  input  \езда 
);

  wire clock_1_out, decoder_1_out0, decoder_1_out1, decoder_1_out2, decoder_1_out3, undriven_3, undriven_4,
       undriven_5, \хвать_out ;
  wire [1:0] undriven_2;
  wire [3:0] undriven;
  wire [4:0] multiplexer_1_out, multiplexer_1_out_2, multiplexer_1_out_3, multiplexer_1_out_4,
       multiplexer_1_out_5, multiplexer_3_out, multiplexer_3_out_2, multiplexer_3_out_3, multiplexer_3_out_4,
       multiplexer_3_out_5, multiplexer_5_out, multiplexer_5_out_2, multiplexer_5_out_3, multiplexer_5_out_4,
       multiplexer_5_out_5, multiplexer_7_out, multiplexer_7_out_2, multiplexer_7_out_3, multiplexer_7_out_4,
       multiplexer_9_out, multiplexer_9_out_2, multiplexer_9_out_3, multiplexer_9_out_4, multiplexer_9_out_5;
  wire [24:0] multiplexer_2_out, multiplexer_4_out, multiplexer_6_out, multiplexer_8_out;
  wire [24:20] multiplexer_7_out_5;

  Clock clock_1 (.out(clock_1_out));
  Button \u_хвать  (.out(\хвать_out ));
  LED led_1 (.in(clock_1_out));
  LED led_2 (.in(\сброс ));
  Decoder #(.select(2), .disabled(0), .enable("false")) decoder_1 (
    .out0(decoder_1_out0), .out1(decoder_1_out1), .out2(decoder_1_out2), .out3(decoder_1_out3),
    .sel(undriven_2));
  LED led_3 (.in(undriven[0]));
  DotMatrix #(.matrixrows(5)) dotmatrix_1 (
    .col0(multiplexer_3_out_5), .col1(multiplexer_3_out_4), .col2(multiplexer_3_out_3),
    .col3(multiplexer_3_out_2), .col4(multiplexer_3_out));
  DotMatrix #(.matrixrows(5)) dotmatrix_2 (
    .col0(multiplexer_1_out_5), .col1(multiplexer_1_out_4), .col2(multiplexer_1_out_3),
    .col3(multiplexer_1_out_2), .col4(multiplexer_1_out));
  Multiplexer #(.width(25), .enable("false")) multiplexer_1 (
    .in0({25{1'b0}}), .in1(multiplexer_2_out),
    .out({multiplexer_1_out_5, multiplexer_1_out_4, multiplexer_1_out_3, multiplexer_1_out_2, multiplexer_1_out}),
    .sel(decoder_1_out0));
  Multiplexer #(.width(25), .enable("false")) multiplexer_2 (
    .in0(25'h1f0843f), .in1(25'h1f0943f), .out(multiplexer_2_out), .sel(undriven_4));
  LED led_4 (.in(undriven[1]));
  LED led_5 (.in(undriven[2]));
  DotMatrix #(.matrixrows(5)) dotmatrix_3 (
    .col0(multiplexer_5_out_5), .col1(multiplexer_5_out_4), .col2(multiplexer_5_out_3),
    .col3(multiplexer_5_out_2), .col4(multiplexer_5_out));
  Multiplexer #(.width(25), .enable("false")) multiplexer_3 (
    .in0({25{1'b0}}), .in1(multiplexer_4_out),
    .out({multiplexer_3_out_5, multiplexer_3_out_4, multiplexer_3_out_3, multiplexer_3_out_2, multiplexer_3_out}),
    .sel(decoder_1_out1));
  Multiplexer #(.width(25), .enable("false")) multiplexer_4 (
    .in0(25'h1f0843f), .in1(25'h1f0943f), .out(multiplexer_4_out), .sel(undriven_4));
  LED led_6 (.in(undriven[3]));
  DotMatrix #(.matrixrows(5)) dotmatrix_4 (
    .col0(multiplexer_7_out_5), .col1(multiplexer_7_out_4), .col2(multiplexer_7_out_3),
    .col3(multiplexer_7_out_2), .col4(multiplexer_7_out));
  Multiplexer #(.width(25), .enable("false")) multiplexer_5 (
    .in0({25{1'b0}}), .in1(multiplexer_6_out),
    .out({multiplexer_5_out_5, multiplexer_5_out_4, multiplexer_5_out_3, multiplexer_5_out_2, multiplexer_5_out}),
    .sel(decoder_1_out2));
  Multiplexer #(.width(25), .enable("false")) multiplexer_6 (
    .in0(25'h1f0843f), .in1(25'h1f0943f), .out(multiplexer_6_out), .sel(undriven_4));
  LED led_7 (.in(undriven_5));
  DotMatrix #(.matrixrows(5)) dotmatrix_5 (
    .col0(multiplexer_9_out_5), .col1(multiplexer_9_out_4), .col2(multiplexer_9_out_3),
    .col3(multiplexer_9_out_2), .col4(multiplexer_9_out));
  Multiplexer #(.width(25), .enable("false")) multiplexer_7 (
    .in0({25{1'b0}}), .in1(multiplexer_8_out),
    .out({multiplexer_7_out_5, multiplexer_7_out_4, multiplexer_7_out_3, multiplexer_7_out_2, multiplexer_7_out}),
    .sel(decoder_1_out3));
  Multiplexer #(.width(25), .enable("false")) multiplexer_8 (
    .in0(25'h1f0843f), .in1(25'h1f0943f), .out(multiplexer_8_out), .sel(undriven_4));
  Multiplexer #(.width(25), .enable("false")) multiplexer_9 (
    .in0(25'h4255c4), .in1({25{1'b0}}),
    .out({multiplexer_9_out_5, multiplexer_9_out_4, multiplexer_9_out_3, multiplexer_9_out_2, multiplexer_9_out}),
    .sel(undriven_3));

  // Notes on the sheet:
  //   КОНВЕЙЕР
endmodule
